# Fritzing sketch main (saved by Fritzing 0.9.3b)
breadboards: 1

parts:
  U1 = Carte NUCLEO H755ZI-Q
  R1 = Photocell (LDR) [package=THT]
  R2 = Resistor [tolerance=±5% resistance=10k package=THT]
  Keypad4x1 = Keypad Membran 4x4  # not connected
  SERVO1 = Tower Pro SG90 servo [part_number=101246]
  M1 = fc-51 [package=THT]

nets:
  5V: U1.5V, SERVO1.+5V
  N1: R1.pin_0, M1.pin2
  N2: R1.pin_1, R2.Pin_0
  N3: R2.Pin_1, SERVO1.GND, M1.pin1

custom parts:
  Carte NUCLEO H755ZI-Q: Carte prototype double coeurs ARM
  Keypad Membran 4x4: Membrane Keypad 4x4 Matrix
  Tower Pro SG90 servo: Original file by John De Cristofaro http://www.adafruit.com/products/1449 Adafruit Feedback Servo (Small) Edited by: e-radionica.com 28/9/2015
